// Digital circuit 24BitALU.dig as structural Verilog
module _24BitALU (
  input  [23:0] A,
  input  [23:0] B,
  input  [3:0] S,
  output [23:0] O,
  output _0,
  output Ca,
  output out_7
);

  wire _24bitin1bit_1_out, Add_ca_out, Add_Carry_ca_out, Decrement_A_ca_out, Increment_A_ca_out,
       Sub_Borrow_ca_out, Sub_ca_out;
  wire [23:0] _24bitnegation_1_o, Add_Carry_re, Add_re, Decrement_A_re, Increment_A_re, Sub_Borrow_re, Sub_re;

  _24BitCalc Decrement_A (
    .x(A), .y({24{1'b0}}), .plus(1'b1), .Ca_in(1'b1), .Re(Decrement_A_re), .Ca_out(Decrement_A_ca_out));
  _24BitParallelAdder Increment_A (
    .X(A), .Y({24{1'b0}}), .Ca_in(1'b1), .Ca_out(Increment_A_ca_out), .re(Increment_A_re));
  _24BitNegation _24bitnegation_1 (.Enable(1'b1), .i(A), .o(_24bitnegation_1_o));
  _24BitCalc Sub_Borrow (.x(A), .y(B), .plus(1'b1), .Ca_in(1'b1), .Re(Sub_Borrow_re), .Ca_out(Sub_Borrow_ca_out));
  Multiplexer #(.Selector_Bits(4), .Bits(24)) multiplexer_1 (
    .sel(S), .in_0(A), .in_1(Add_re), .in_2(Add_Carry_re), .in_3(Sub_re), .in_4(Sub_Borrow_re),
    .in_5(_24bitnegation_1_o), .in_6(Increment_A_re), .in_7(Decrement_A_re), .in_8({24{1'b0}}),
    .in_9({24{1'b0}}), .in_10({24{1'b0}}), .in_11({24{1'b0}}), .in_12({24{1'b0}}), .in_13({24{1'b0}}),
    .in_14({24{1'b0}}), .in_15({24{1'b0}}), .out(O));
  _24BitCalc Sub (.x(A), .y(B), .plus(1'b1), .Ca_in(1'b0), .Re(Sub_re), .Ca_out(Sub_ca_out));
  _24BitParallelAdder Add_Carry (.X(A), .Y(B), .Ca_in(1'b1), .Ca_out(Add_Carry_ca_out), .re(Add_Carry_re));
  _24BitParallelAdder Add (.X(A), .Y(B), .Ca_in(1'b0), .Ca_out(Add_ca_out), .re(Add_re));
  Multiplexer #(.Selector_Bits(4)) multiplexer_2 (
    .sel(S), .in_0(1'b0), .in_1(Add_ca_out), .in_2(Add_Carry_ca_out), .in_3(Sub_ca_out),
    .in_4(Sub_Borrow_ca_out), .in_5(1'b0), .in_6(Increment_A_ca_out), .in_7(Decrement_A_ca_out), .in_8(1'b0),
    .in_9(1'b0), .in_10(1'b0), .in_11(1'b0), .in_12(1'b0), .in_13(1'b0), .in_14(1'b0), .in_15(1'b0), .out(Ca));
  _24BitIn1Bit _24bitin1bit_1 (.in(O), .out(_24bitin1bit_1_out));
  not not_1 (_0, _24bitin1bit_1_out);
  _24BitIsNegativ _24bitisnegativ_1 (.I(O), .IsNeg(out_7));
endmodule
