// Digital circuit 8BitProzessor MitRam.dig as structural Verilog
module _8BitProzessor_MitRam (
  input  [23:0] DataBus_in,
  input  RDY,
  input  Clock_M,
  input  Clock_A,
  input  Enable,
  input  Enable_2,
  output [23:0] DataBus_out,
  output [23:0] AddBus,
  output WR,
  output RD,
  output [7:0] IterationPoint,
  output [23:0] A,
  output [23:0] B,
  output [23:0] Y,
  output [23:0] R_1,
  output [23:0] IP,
  output [23:0] IR,
  output [23:0] MAR,
  output [23:0] MDR_OP,
  output [23:0] R_2,
  output [23:0] R_3,
  output [23:0] R_0,
  output [23:0] Akk,
  output [7:0] IterationPoint_2,
  output [23:0] A_2,
  output [23:0] B_2,
  output [23:0] Y_2,
  output [23:0] R_5,
  output [23:0] IP_2,
  output [7:0] IR_2,
  output [23:0] MAR_2,
  output [7:0] MDR_OP_2,
  output [23:0] R_6,
  output [23:0] R_7,
  output [23:0] R_4,
  output [23:0] Akk_2,
  output [23:0] Bus,
  output [23:0] MDR_A0,
  output [7:0] MDR_A0_2,
  output [23:0] MDR_A1,
  output [7:0] MDR_A1_2,
  output [23:0] MDR,
  output [23:0] MDR_2
);

  wire _24bitin1bit_1_out, ALU_p1, ALU_p5, ALU_p6, ALU_p7, and_1_out, controlunit_1_p1, controlunit_1_p2,
       controlunit_1_p3, controlunit_1_p4, controlunit_1_p5, controlunit_1_p6, controlunit_1_p9,
       controlunit_1_p10, controlunit_1_p11, controlunit_1_p12, controlunit_1_p13, controlunit_1_p16,
       controlunit_1_p17, controlunit_1_p18, controlunit_1_p19, controlunit_1_p24, controlunit_1_p28,
       IR_InstructionRegister_p2, not_1_out, Y_p2;
  wire [1:0] controlunit_1_p14;
  wire [7:0] or_1_out;
  wire [15:8] or_1_out_2;
  wire [23:0] ALU_p3, demultiplexer_1_out_0, demultiplexer_1_out_1, demultiplexer_1_out_2,
       demultiplexer_1_out_3, driver_10_out, multiplexer_1_out, multiplexer_2_out, ramasync_1_q;
  wire [23:16] or_1_out_3;

  Multiplexer #(.Bits(24)) multiplexer_1 (.sel(Enable_2), .in_0({24{1'b0}}), .in_1(24'h10000), .out(multiplexer_1_out));
  assign Bus = controlunit_1_p2 ? DataBus_out : 24'bz;  // Driver driver_1
  assign Bus = controlunit_1_p3 ? MDR_A1 : 24'bz;  // Driver driver_2
  assign Bus = controlunit_1_p4 ? MDR_A0 : 24'bz;  // Driver driver_3
  assign Bus = controlunit_1_p5 ? MDR_OP : 24'bz;  // Driver driver_4
  assign Bus = controlunit_1_p9 ? IR : 24'bz;  // Driver driver_5
  assign Bus = controlunit_1_p11 ? IP : 24'bz;  // Driver driver_6
  assign Bus = controlunit_1_p13 ? multiplexer_2_out : 24'bz;  // Driver driver_7
  assign Bus = controlunit_1_p16 ? Y : 24'bz;  // Driver driver_8
  assign Bus = controlunit_1_p19 ? Akk : 24'bz;  // Driver driver_9
  Demultiplexer #(.Selector_Bits(2), .Bits(24)) demultiplexer_1 (
    .sel(controlunit_1_p14), .in(Bus), .out_0(demultiplexer_1_out_0), .out_1(demultiplexer_1_out_1),
    .out_2(demultiplexer_1_out_2), .out_3(demultiplexer_1_out_3));
  assign {or_1_out_3, or_1_out_2, or_1_out} = driver_10_out | multiplexer_1_out | DataBus_in;  // Or or_1, 24 bits wide
  _24_BitRegister MDR_A2 (.I({or_1_out_3, or_1_out_2, or_1_out}), .W(controlunit_1_p1), .R(1'b1), .O(DataBus_out));
  _24_BitRegister u_MDR_A1 (.I({{16{1'b0}}, or_1_out}), .W(controlunit_1_p1), .R(1'b1), .O(MDR_A1));
  _24_BitRegister u_MDR_A0 (.I({{8{1'b0}}, or_1_out_2, {8{1'b0}}}), .W(controlunit_1_p1), .R(1'b1), .O(MDR_A0));
  _24_BitRegister u_MDR_OP (.I({or_1_out_3, {16{1'b0}}}), .W(controlunit_1_p1), .R(1'b1), .O(MDR_OP));
  _24_BitRegister u_MAR (.I(Bus), .W(controlunit_1_p6), .R(1'b1), .O(AddBus));
  // _24_BitRegister IR_InstructionRegister: pin names not known; wires that end beside it: 1'b1, IR_InstructionRegister_p2, IR, Bus
  _24_BitRegister IP_InstructionPointer (.I(Bus), .W(controlunit_1_p10), .R(1'b1), .O(IP));
  // _24_BitRegister Y: pin names not known; wires that end beside it: 1'b1, Y_p2, Y, Bus
  _24_BitRegister _24_bitregister_1 (.I(ALU_p3), .W(controlunit_1_p18), .R(1'b1), .O(Akk));
  _24_BitRegister u_A (.I(Bus), .W(controlunit_1_p18), .R(1'b1), .O(A));
  // _24BitALU ALU: pin names not known; wires that end beside it: ALU_p1, A, ALU_p3, B, ALU_p5, ALU_p6, ALU_p7
  _24_BitRegister u_R_0 (.I(demultiplexer_1_out_0), .W(controlunit_1_p12), .R(1'b1), .O(R_3));
  _24_BitRegister u_R_1 (.I(demultiplexer_1_out_1), .W(controlunit_1_p12), .R(1'b1), .O(R_2));
  _24_BitRegister u_R_2 (.I(demultiplexer_1_out_2), .W(controlunit_1_p12), .R(1'b1), .O(R_1));
  _24_BitRegister u_R_3 (.I(demultiplexer_1_out_3), .W(controlunit_1_p12), .R(1'b1), .O(R_0));
  _24_BitRegister u_B (.I(Bus), .W(controlunit_1_p17), .R(1'b1), .O(B));
  RAMAsync #(.AddrBits(8), .Bits(24), .isProgramMemory("true")) ramasync_1 (
    .A(AddBus[7:0]), .D(DataBus_out), .we(WR), .Q(ramasync_1_q));
  _24BitIn1Bit _24bitin1bit_1 (.in(ramasync_1_q), .out(_24bitin1bit_1_out));
  not not_1 (not_1_out, _24bitin1bit_1_out);
  Multiplexer #(.Selector_Bits(2), .Bits(24)) multiplexer_2 (
    .sel(controlunit_1_p14), .in_0(R_3), .in_1(R_2), .in_2(R_1), .in_3(R_0), .out(multiplexer_2_out));
  assign driver_10_out = RD ? ramasync_1_q : 24'bz;  // Driver driver_10
  // ControlUnit controlunit_1: pin names not known; wires that end beside it: controlunit_1_p1, controlunit_1_p2, controlunit_1_p3, controlunit_1_p4, controlunit_1_p5, controlunit_1_p6, IR, IR_InstructionRegister_p2, controlunit_1_p9, controlunit_1_p10, controlunit_1_p11, controlunit_1_p12, controlunit_1_p13, controlunit_1_p14, Y_p2, controlunit_1_p16, controlunit_1_p17, controlunit_1_p18, controlunit_1_p19, ALU_p1, ALU_p5, ALU_p6, ALU_p7, controlunit_1_p24, IterationPoint, WR, RD, controlunit_1_p28
  or or_2 (controlunit_1_p28, RDY, not_1_out);
  and and_1 (and_1_out, Clock_A, Enable);
  or or_3 (controlunit_1_p24, Clock_M, and_1_out);

  assign A_2 = A;
  assign Akk_2 = Akk;
  assign B_2 = B;
  assign IP_2 = IP;
  assign IR_2 = IR[23:16];
  assign IterationPoint_2 = IterationPoint;
  assign MAR = AddBus;
  assign MAR_2 = AddBus;
  assign MDR = DataBus_out;
  assign MDR_2 = DataBus_out;
  assign MDR_A0_2 = MDR_A0[15:8];
  assign MDR_A1_2 = MDR_A1[7:0];
  assign MDR_OP_2 = MDR_OP[23:16];
  assign R_4 = R_0;
  assign R_5 = R_1;
  assign R_6 = R_2;
  assign R_7 = R_3;
  assign Y_2 = Y;

  // Notes on the sheet:
  //   CPU
endmodule
