// Digital circuit 8BitProzessor.dig as structural Verilog
module _8BitProzessor (
  input  [23:0] DataBus_in,
  input  RDY,
  input  Clock,
  output [23:0] DataBus_out,
  output [23:0] AddBus,
  output WR,
  output RD
);

  wire _8bitin1bit_1_out, ALU__0, ALU_ca, ALU_out_7, controlunit_1_a_in, controlunit_1_alu_out,
       controlunit_1_b_in, controlunit_1_ip_in, controlunit_1_ip_out, controlunit_1_ir_in,
       controlunit_1_ir_op_out, controlunit_1_mar_in, controlunit_1_mdr_inbus, controlunit_1_mdr_insplit,
       controlunit_1_mdr_out, controlunit_1_mdr_outa0, controlunit_1_mdr_outa1, controlunit_1_mdr_outop,
       controlunit_1_r_in, controlunit_1_r_out, controlunit_1_y_in, controlunit_1_y_out, or_1_out;
  wire [1:0] controlunit_1_sr_eq_ropx;
  wire [3:0] controlunit_1_f_eq_x, delay_1_out;
  wire [23:0] _24_bitregister_1_o, A_o, ALU_o, B_o, demultiplexer_1_out_0, demultiplexer_1_out_1,
       demultiplexer_1_out_2, demultiplexer_1_out_3, driver_1_out, IP_InstructionPointer_o,
       IR_InstructionRegister_o, MDR_A0_o, MDR_A1_o, MDR_OP_o, multiplexer_1_out, multiplexer_2_out, R_4_o,
       R_5_o, R_6_o, R_7_o, Y_o;

  assign driver_1_out = controlunit_1_mdr_out ? DataBus_out : 24'bz;  // Driver driver_1
  assign driver_1_out = controlunit_1_mdr_outa1 ? MDR_A0_o : 24'bz;  // Driver driver_2
  assign driver_1_out = controlunit_1_mdr_outa0 ? MDR_A1_o : 24'bz;  // Driver driver_3
  assign driver_1_out = controlunit_1_mdr_outop ? MDR_OP_o : 24'bz;  // Driver driver_4
  assign driver_1_out = controlunit_1_ir_op_out ? IR_InstructionRegister_o : 24'bz;  // Driver driver_5
  assign driver_1_out = controlunit_1_ip_out ? IP_InstructionPointer_o : 24'bz;  // Driver driver_6
  assign driver_1_out = controlunit_1_r_out ? multiplexer_2_out : 24'bz;  // Driver driver_7
  assign driver_1_out = controlunit_1_y_out ? Y_o : 24'bz;  // Driver driver_8
  assign driver_1_out = controlunit_1_alu_out ? _24_bitregister_1_o : 24'bz;  // Driver driver_9
  Demultiplexer #(.Selector_Bits(2), .Bits(24)) demultiplexer_1 (
    .sel(controlunit_1_sr_eq_ropx), .in(driver_1_out), .out_0(demultiplexer_1_out_0),
    .out_1(demultiplexer_1_out_1), .out_2(demultiplexer_1_out_2), .out_3(demultiplexer_1_out_3));
  Multiplexer #(.Bits(24)) multiplexer_1 (
    .sel(controlunit_1_mdr_inbus), .in_0(DataBus_in), .in_1(driver_1_out), .out(multiplexer_1_out));
  _24_BitRegister MDR (.I(multiplexer_1_out), .W(or_1_out), .R(1'b1), .O(DataBus_out));
  _24_BitRegister MDR_A0 (.I({{16{1'b0}}, DataBus_in[7:0]}), .W(controlunit_1_mdr_insplit), .R(1'b1), .O(MDR_A0_o));
  _24_BitRegister MDR_A1 (.I({{16{1'b0}}, DataBus_in[15:8]}), .W(controlunit_1_mdr_insplit), .R(1'b1), .O(MDR_A1_o));
  _24_BitRegister MDR_OP (.I({{16{1'b0}}, DataBus_in[23:16]}), .W(controlunit_1_mdr_insplit), .R(1'b1), .O(MDR_OP_o));
  _24_BitRegister MAR (.I(driver_1_out), .W(controlunit_1_mar_in), .R(1'b1), .O(AddBus));
  _24_BitRegister IR_InstructionRegister (
    .I(driver_1_out), .W(controlunit_1_ir_in), .R(1'b1), .O(IR_InstructionRegister_o));
  _24_BitRegister IP_InstructionPointer (
    .I(driver_1_out), .W(controlunit_1_ip_in), .R(1'b1), .O(IP_InstructionPointer_o));
  _24_BitRegister Y (.I(driver_1_out), .W(controlunit_1_y_in), .R(1'b1), .O(Y_o));
  Delay #(.Bits(4), .delayTime(2)) delay_1 (.in(controlunit_1_f_eq_x), .out(delay_1_out));
  _24_BitRegister _24_bitregister_1 (.I(ALU_o), .W(_8bitin1bit_1_out), .R(1'b1), .O(_24_bitregister_1_o));
  _24_BitRegister A (.I(driver_1_out), .W(controlunit_1_a_in), .R(1'b1), .O(A_o));
  _24BitALU ALU (.A(A_o), .B(B_o), .S(delay_1_out), .O(ALU_o), .Ca(ALU_ca), ._0(ALU__0), .out_7(ALU_out_7));
  _8BitIn1Bit _8bitin1bit_1 (.in({4'b0000, controlunit_1_f_eq_x}), .out(_8bitin1bit_1_out));
  _24_BitRegister R_4 (.I(demultiplexer_1_out_0), .W(controlunit_1_r_in), .R(1'b1), .O(R_4_o));
  _24_BitRegister R_5 (.I(demultiplexer_1_out_1), .W(controlunit_1_r_in), .R(1'b1), .O(R_5_o));
  _24_BitRegister R_6 (.I(demultiplexer_1_out_2), .W(controlunit_1_r_in), .R(1'b1), .O(R_6_o));
  _24_BitRegister R_7 (.I(demultiplexer_1_out_3), .W(controlunit_1_r_in), .R(1'b1), .O(R_7_o));
  _24_BitRegister B (.I(driver_1_out), .W(controlunit_1_b_in), .R(1'b1), .O(B_o));
  or or_1 (or_1_out, RD, controlunit_1_mdr_inbus);
  Multiplexer #(.Selector_Bits(2), .Bits(24)) multiplexer_2 (
    .sel(controlunit_1_sr_eq_ropx), .in_0(R_4_o), .in_1(R_5_o), .in_2(R_6_o), .in_3(R_7_o),
    .out(multiplexer_2_out));
  ControlUnit controlunit_1 (
    .MDR_inBus(controlunit_1_mdr_inbus), .MDR_inSplit(controlunit_1_mdr_insplit),
    .MDR_out(controlunit_1_mdr_out), .MDR_outA1(controlunit_1_mdr_outa1),
    .MDR_outA0(controlunit_1_mdr_outa0), .MDR_outOP(controlunit_1_mdr_outop), .MAR_in(controlunit_1_mar_in),
    .Decodierung(IR_InstructionRegister_o), .IR_in(controlunit_1_ir_in), .IR_op_out(controlunit_1_ir_op_out),
    .IP_in(controlunit_1_ip_in), .IP_out(controlunit_1_ip_out), .R_in(controlunit_1_r_in),
    .R_out(controlunit_1_r_out), .SR_eq_ROPx(controlunit_1_sr_eq_ropx), .Y_in(controlunit_1_y_in),
    .Y_out(controlunit_1_y_out), .B_in(controlunit_1_b_in), .A_in(controlunit_1_a_in),
    .ALU_out(controlunit_1_alu_out), .F_eq_x(controlunit_1_f_eq_x), .Ca(ALU_ca), ._0(ALU__0),
    .in_21(ALU_out_7), .WR(WR), .RD(RD), .RDY(RDY), .clock(Clock));  // open: IterationPoint

  // Notes on the sheet:
  //   CPU
  //   You can Move The Inputs and Outputs anywhere you want them to :3
endmodule
