// Digital circuit 8BitProzessorMitSelfMadeRamVerbindung.dig as structural Verilog
module _8BitProzessorMitSelfMadeRamVerbindung (
  input  [23:0] DataBus_in,
  input  RDY,
  input  C_A_0,
  input  C_A_1,
  input  [7:0] AddBus_in,
  output [23:0] DataBus_out,
  output [23:0] AddBus,
  output WR,
  output RD,
  output [7:0] IterationPoint,
  output [23:0] A,
  output [23:0] B,
  output [23:0] Y,
  output [23:0] R_1,
  output [23:0] IP,
  output [23:0] IR,
  output [23:0] MAR,
  output [23:0] MDR,
  output [23:0] R_2,
  output [23:0] R_3,
  output [23:0] R_0,
  output [23:0] Akk,
  output [23:0] O,
  output [7:0] Add,
  output [23:0] I,
  output [23:0] A_2,
  output [23:0] B_2,
  output [23:0] Y_2,
  output [23:0] R_5,
  output [23:0] IP_2,
  output [23:0] IR_2,
  output [23:0] MAR_2,
  output [23:0] MDR_2,
  output [23:0] R_6,
  output [23:0] R_7,
  output [23:0] R_4,
  output [23:0] Akk_2,
  output [7:0] IterationPoint_2
);

  wire _8bitin1bit_1_out, ALU_p1, ALU_p5, ALU_p6, ALU_p7, controlunit_1_p1, controlunit_1_p2,
       controlunit_1_p3, controlunit_1_p5, controlunit_1_p6, controlunit_1_p7, controlunit_1_p8,
       controlunit_1_p9, controlunit_1_p10, controlunit_1_p12, controlunit_1_p13, controlunit_1_p14,
       controlunit_1_p15, controlunit_1_p16, controlunit_1_p25, multiplexer_1_out, or_2_out, or_3_out,
       or_7_out, prebuiltramconfig_1_rdy, prebuiltramconfig_1_w;
  wire [1:0] controlunit_1_p11;
  wire [7:0] multiplexer_4_out, multiplexer_5_out, or_6_out, prebuiltramconfig_1_add;
  wire [23:0] ALU_p3, demultiplexer_1_out_0, demultiplexer_1_out_1, demultiplexer_1_out_2,
       demultiplexer_1_out_3, driver_1_out, multiplexer_2_out, multiplexer_3_out, or_1_out,
       prebuiltramconfig_1_i;

  assign driver_1_out = controlunit_1_p2 ? DataBus_out : 24'bz;  // Driver driver_1
  assign driver_1_out = controlunit_1_p6 ? IR : 24'bz;  // Driver driver_2
  assign driver_1_out = controlunit_1_p8 ? IP : 24'bz;  // Driver driver_3
  assign driver_1_out = controlunit_1_p10 ? multiplexer_2_out : 24'bz;  // Driver driver_4
  assign driver_1_out = controlunit_1_p13 ? Y : 24'bz;  // Driver driver_5
  assign driver_1_out = controlunit_1_p16 ? Akk : 24'bz;  // Driver driver_6
  Demultiplexer #(.Selector_Bits(2), .Bits(24)) demultiplexer_1 (
    .sel(controlunit_1_p11), .in(driver_1_out), .out_0(demultiplexer_1_out_0), .out_1(demultiplexer_1_out_1),
    .out_2(demultiplexer_1_out_2), .out_3(demultiplexer_1_out_3));
  assign or_1_out = DataBus_in | O | driver_1_out;  // Or or_1, 24 bits wide
  _24_BitRegister u_MDR (.I(or_1_out), .W(controlunit_1_p1), .R(1'b1), .O(DataBus_out));
  _24_BitRegister u_MAR (.I(driver_1_out), .W(controlunit_1_p3), .R(1'b1), .O(AddBus));
  _24_BitRegister IR_InstructionRegister (.I(driver_1_out), .W(controlunit_1_p5), .R(1'b1), .O(IR));
  _24_BitRegister IP_InstructionPointer (.I(driver_1_out), .W(controlunit_1_p7), .R(1'b1), .O(IP));
  _24_BitRegister u_Y (.I(driver_1_out), .W(controlunit_1_p12), .R(1'b1), .O(Y));
  _24_BitRegister _24_bitregister_1 (.I(ALU_p3), .W(controlunit_1_p15), .R(1'b1), .O(Akk));
  _24_BitRegister u_A (.I(driver_1_out), .W(controlunit_1_p15), .R(1'b1), .O(A));
  // _24BitALU ALU: pin names not known; wires that end beside it: ALU_p1, A, ALU_p3, B, ALU_p5, ALU_p6, ALU_p7
  or or_2 (or_2_out, prebuiltramconfig_1_w, multiplexer_1_out);
  Multiplexer multiplexer_1 (.sel(prebuiltramconfig_1_rdy), .in_0(1'b0), .in_1(WR), .out(multiplexer_1_out));
  _24_BitRegister u_R_0 (.I(demultiplexer_1_out_0), .W(controlunit_1_p9), .R(1'b1), .O(R_3));
  _24_BitRegister u_R_1 (.I(demultiplexer_1_out_1), .W(controlunit_1_p9), .R(1'b1), .O(R_2));
  _24_BitRegister u_R_2 (.I(demultiplexer_1_out_2), .W(controlunit_1_p9), .R(1'b1), .O(R_1));
  _24_BitRegister u_R_3 (.I(demultiplexer_1_out_3), .W(controlunit_1_p9), .R(1'b1), .O(R_0));
  _24_BitRegister u_B (.I(driver_1_out), .W(controlunit_1_p14), .R(1'b1), .O(B));
  or or_3 (or_3_out, 1'b0, RD);
  _736ByteRam _736byteram_1 (.I(I), .Add(Add), .W(or_2_out), .R(or_3_out), .O(O));
  Multiplexer #(.Selector_Bits(2), .Bits(24)) multiplexer_2 (
    .sel(controlunit_1_p11), .in_0(R_3), .in_1(R_2), .in_2(R_1), .in_3(R_0), .out(multiplexer_2_out));
  assign I = prebuiltramconfig_1_i | multiplexer_3_out;  // Or or_4, 24 bits wide
  Multiplexer #(.Bits(24)) multiplexer_3 (
    .sel(prebuiltramconfig_1_rdy), .in_0({24{1'b0}}), .in_1(DataBus_out), .out(multiplexer_3_out));
  Multiplexer #(.Bits(8)) multiplexer_4 (
    .sel(_8bitin1bit_1_out), .in_0(AddBus[7:0]), .in_1({8{1'b0}}), .out(multiplexer_4_out));
  assign Add = prebuiltramconfig_1_add | multiplexer_5_out;  // Or or_5, 8 bits wide
  Multiplexer #(.Bits(8)) multiplexer_5 (
    .sel(prebuiltramconfig_1_rdy), .in_0({8{1'b0}}), .in_1(or_6_out), .out(multiplexer_5_out));
  assign or_6_out = multiplexer_4_out | AddBus_in;  // Or or_6, 8 bits wide
  _8BitIn1Bit _8bitin1bit_1 (.in(AddBus_in), .out(_8bitin1bit_1_out));
  // ControlUnit controlunit_1: pin names not known; wires that end beside it: controlunit_1_p1, controlunit_1_p2, controlunit_1_p3, IR, controlunit_1_p5, controlunit_1_p6, controlunit_1_p7, controlunit_1_p8, controlunit_1_p9, controlunit_1_p10, controlunit_1_p11, controlunit_1_p12, controlunit_1_p13, controlunit_1_p14, controlunit_1_p15, controlunit_1_p16, ALU_p1, ALU_p5, ALU_p6, ALU_p7, C_A_1, IterationPoint, WR, RD, controlunit_1_p25
  PreBuiltRamConfig prebuiltramconfig_1 (
    .C_M(1'b0), .C_A(C_A_0), .I(prebuiltramconfig_1_i), .Add(prebuiltramconfig_1_add),
    .W(prebuiltramconfig_1_w), .RDY(prebuiltramconfig_1_rdy));
  or or_7 (or_7_out, prebuiltramconfig_1_rdy, 1'b0);
  or or_8 (controlunit_1_p25, or_7_out, RDY);

  assign A_2 = A;
  assign Akk_2 = Akk;
  assign B_2 = B;
  assign IP_2 = IP;
  assign IR_2 = IR;
  assign IterationPoint_2 = IterationPoint;
  assign MAR = AddBus;
  assign MAR_2 = AddBus;
  assign MDR = DataBus_out;
  assign MDR_2 = DataBus_out;
  assign R_4 = R_0;
  assign R_5 = R_1;
  assign R_6 = R_2;
  assign R_7 = R_3;
  assign Y_2 = Y;

  // Notes on the sheet:
  //   CPU
endmodule
