// Digital circuit 8BitProzessorVisualization.dig as structural Verilog
module _8BitProzessorVisualization (
  input  [23:0] DataBus_in,
  input  RDY,
  input  Clock_M,
  input  Clock_A,
  input  Enable,
  input  Enable_0,
  input  Enable_1,
  output [23:0] DataBus_out,
  output [23:0] AddBus,
  output WR,
  output RD,
  output [7:0] IterationPoint,
  output [23:0] A,
  output [23:0] B,
  output [23:0] Y,
  output [23:0] R_1,
  output [23:0] IP,
  output [23:0] IR,
  output [23:0] MAR,
  output [23:0] MDR_OP,
  output [23:0] R_2,
  output [23:0] R_3,
  output [23:0] R_0,
  output [23:0] Akk,
  output [7:0] IterationPoint_2,
  output [23:0] A_2,
  output [23:0] B_2,
  output [23:0] Y_2,
  output [23:0] R_5,
  output [23:0] IP_2,
  output [7:0] IR_2,
  output [23:0] MAR_2,
  output [7:0] MDR_OP_2,
  output [23:0] R_6,
  output [23:0] R_7,
  output [23:0] R_4,
  output [23:0] Akk_2,
  output [23:0] Bus,
  output [23:0] MDR_A0,
  output [7:0] MDR_A0_2,
  output [23:0] MDR_A1,
  output [7:0] MDR_A1_2,
  output [23:0] MDR,
  output [23:0] MDR_2
);

  wire _8bitin1bit_1_out, _24bitin1bit_1_out, ALU__0, ALU_ca, ALU_out_7, and_1_out, controlunit_1_a_in,
       controlunit_1_alu_out, controlunit_1_b_in, controlunit_1_ip_in, controlunit_1_ip_out,
       controlunit_1_ir_in, controlunit_1_ir_op_out, controlunit_1_mar_in, controlunit_1_mdr_inbus,
       controlunit_1_mdr_insplit, controlunit_1_mdr_out, controlunit_1_mdr_outa0, controlunit_1_mdr_outa1,
       controlunit_1_mdr_outop, controlunit_1_r_in, controlunit_1_r_out, controlunit_1_y_in,
       controlunit_1_y_out, not_1_out, or_2_out, or_3_out, or_4_out;
  wire [1:0] controlunit_1_sr_eq_ropx;
  wire [3:0] controlunit_1_f_eq_x, delay_1_out;
  wire [7:0] or_1_out, or_1_out_2, or_1_out_3;
  wire [23:0] ALU_o, demultiplexer_1_out_0, demultiplexer_1_out_1, demultiplexer_1_out_2,
       demultiplexer_1_out_3, multiplexer_1_out, multiplexer_2_out, multiplexer_3_out, pulldown_1_out,
       ramasync_1_q;

  Multiplexer #(.Selector_Bits(2), .Bits(24)) multiplexer_1 (
    .sel({Enable_1, Enable_0}), .in_0({24{1'b0}}), .in_1(24'h30504), .in_2(24'h3), .in_3(24'h6),
    .out(multiplexer_1_out));
  assign Bus = controlunit_1_mdr_out ? DataBus_out : 24'bz;  // Driver driver_1
  assign Bus = controlunit_1_mdr_outa0 ? MDR_A1 : 24'bz;  // Driver driver_2
  assign Bus = controlunit_1_mdr_outa1 ? MDR_A0 : 24'bz;  // Driver driver_3
  assign Bus = controlunit_1_mdr_outop ? MDR_OP : 24'bz;  // Driver driver_4
  assign Bus = controlunit_1_ir_op_out ? IR : 24'bz;  // Driver driver_5
  assign Bus = controlunit_1_ip_out ? IP : 24'bz;  // Driver driver_6
  assign Bus = controlunit_1_r_out ? multiplexer_3_out : 24'bz;  // Driver driver_7
  assign Bus = controlunit_1_y_out ? Y : 24'bz;  // Driver driver_8
  assign Bus = controlunit_1_alu_out ? Akk : 24'bz;  // Driver driver_9
  Demultiplexer #(.Selector_Bits(2), .Bits(24)) demultiplexer_1 (
    .sel(controlunit_1_sr_eq_ropx), .in(Bus), .out_0(demultiplexer_1_out_0), .out_1(demultiplexer_1_out_1),
    .out_2(demultiplexer_1_out_2), .out_3(demultiplexer_1_out_3));
  assign {or_1_out_3, or_1_out_2, or_1_out} = pulldown_1_out | multiplexer_1_out | DataBus_in;  // Or or_1, 24 bits wide
  Multiplexer #(.Bits(24)) multiplexer_2 (
    .sel(controlunit_1_mdr_inbus), .in_0({or_1_out_3, or_1_out_2, or_1_out}), .in_1(Bus),
    .out(multiplexer_2_out));
  _24_BitRegister u_MDR (.I(multiplexer_2_out), .W(or_2_out), .R(1'b1), .O(DataBus_out));
  _24_BitRegister u_MDR_A1 (.I({{16{1'b0}}, or_1_out}), .W(controlunit_1_mdr_insplit), .R(1'b1), .O(MDR_A1));
  _24_BitRegister u_MDR_A0 (.I({{16{1'b0}}, or_1_out_2}), .W(controlunit_1_mdr_insplit), .R(1'b1), .O(MDR_A0));
  _24_BitRegister u_MDR_OP (.I({{16{1'b0}}, or_1_out_3}), .W(controlunit_1_mdr_insplit), .R(1'b1), .O(MDR_OP));
  _24_BitRegister u_MAR (.I(Bus), .W(controlunit_1_mar_in), .R(1'b1), .O(AddBus));
  _24_BitRegister IR_InstructionRegister (.I(Bus), .W(controlunit_1_ir_in), .R(1'b1), .O(IR));
  _24_BitRegister IP_InstructionPointer (.I(Bus), .W(controlunit_1_ip_in), .R(1'b1), .O(IP));
  _24_BitRegister u_Y (.I(Bus), .W(controlunit_1_y_in), .R(1'b1), .O(Y));
  Delay #(.Bits(4), .delayTime(2)) delay_1 (.in(controlunit_1_f_eq_x), .out(delay_1_out));
  _24_BitRegister _24_bitregister_1 (.I(ALU_o), .W(_8bitin1bit_1_out), .R(1'b1), .O(Akk));
  _24_BitRegister u_A (.I(Bus), .W(controlunit_1_a_in), .R(1'b1), .O(A));
  _24BitALU ALU (.A(A), .B(B), .S(delay_1_out), .O(ALU_o), .Ca(ALU_ca), ._0(ALU__0), .out_7(ALU_out_7));
  _8BitIn1Bit _8bitin1bit_1 (.in({4'b0000, controlunit_1_f_eq_x}), .out(_8bitin1bit_1_out));
  _24_BitRegister u_R_0 (.I(demultiplexer_1_out_0), .W(controlunit_1_r_in), .R(1'b1), .O(R_3));
  _24_BitRegister u_R_1 (.I(demultiplexer_1_out_1), .W(controlunit_1_r_in), .R(1'b1), .O(R_2));
  _24_BitRegister u_R_2 (.I(demultiplexer_1_out_2), .W(controlunit_1_r_in), .R(1'b1), .O(R_1));
  _24_BitRegister u_R_3 (.I(demultiplexer_1_out_3), .W(controlunit_1_r_in), .R(1'b1), .O(R_0));
  _24_BitRegister u_B (.I(Bus), .W(controlunit_1_b_in), .R(1'b1), .O(B));
  RAMAsync #(.AddrBits(8), .Bits(24)) ramasync_1 (.A(AddBus[7:0]), .D(DataBus_out), .we(WR), .Q(ramasync_1_q));
  or or_2 (or_2_out, RD, controlunit_1_mdr_inbus);
  Multiplexer #(.Selector_Bits(2), .Bits(24)) multiplexer_3 (
    .sel(controlunit_1_sr_eq_ropx), .in_0(R_3), .in_1(R_2), .in_2(R_1), .in_3(R_0), .out(multiplexer_3_out));
  PullDown #(.Bits(24)) pulldown_1 (.out(pulldown_1_out));
  assign pulldown_1_out = RD ? ramasync_1_q : 24'bz;  // Driver driver_10
  _24BitIn1Bit _24bitin1bit_1 (.in(pulldown_1_out), .out(_24bitin1bit_1_out));
  not not_1 (not_1_out, _24bitin1bit_1_out);
  ControlUnit controlunit_1 (
    .MDR_inBus(controlunit_1_mdr_inbus), .MDR_inSplit(controlunit_1_mdr_insplit),
    .MDR_out(controlunit_1_mdr_out), .MDR_outA0(controlunit_1_mdr_outa0),
    .MDR_outA1(controlunit_1_mdr_outa1), .MDR_outOP(controlunit_1_mdr_outop), .MAR_in(controlunit_1_mar_in),
    .Decodierung(IR), .IR_in(controlunit_1_ir_in), .IR_op_out(controlunit_1_ir_op_out),
    .IP_in(controlunit_1_ip_in), .IP_out(controlunit_1_ip_out), .R_in(controlunit_1_r_in),
    .R_out(controlunit_1_r_out), .SR_eq_ROPx(controlunit_1_sr_eq_ropx), .Y_in(controlunit_1_y_in),
    .Y_out(controlunit_1_y_out), .B_in(controlunit_1_b_in), .A_in(controlunit_1_a_in),
    .ALU_out(controlunit_1_alu_out), .F_eq_x(controlunit_1_f_eq_x), .Ca(ALU_ca), ._0(ALU__0),
    .in_21(ALU_out_7), .WR(WR), .RD(RD), .RDY(or_3_out), .clock(or_4_out), .IterationPoint(IterationPoint));
  or or_3 (or_3_out, RDY, not_1_out);
  and and_1 (and_1_out, Clock_A, Enable);
  or or_4 (or_4_out, Clock_M, and_1_out);

  assign A_2 = A;
  assign Akk_2 = Akk;
  assign B_2 = B;
  assign IP_2 = IP;
  assign IR_2 = IR[7:0];
  assign IterationPoint_2 = IterationPoint;
  assign MAR = AddBus;
  assign MAR_2 = AddBus;
  assign MDR = DataBus_out;
  assign MDR_2 = DataBus_out;
  assign MDR_A0_2 = MDR_A0[7:0];
  assign MDR_A1_2 = MDR_A1[7:0];
  assign MDR_OP_2 = MDR_OP[7:0];
  assign R_4 = R_0;
  assign R_5 = R_1;
  assign R_6 = R_2;
  assign R_7 = R_3;
  assign Y_2 = Y;

  // Notes on the sheet:
  //   CPU
  //   24 Bits -> 8Bit OP , 8BitA0, 8BitA1
  //   00 - 0
  //   03 - Reg0 = Reg0 + Reg1
  //   08 - JumpTo  Reg1 (global)
  //   10 - JumpTo Reg1 if Reg0 is Pos
endmodule
