// Digital circuit 8BitSequenzenzähler.dig as structural Verilog
module \_8BitSequenzenzähler  (
  input  C,
  input  [7:0] JT,
  input  R,
  output [7:0] Add,
  output Ca
);

  wire _8bitin1bit_1_out, _8bitin1bit_2_out, multiplexer_3_out, not_1_out, not_2_out, not_3_out, or_1_out;
  wire [7:0] _8_bitregister_1_o, _8bitparalleladder_1_re, multiplexer_1_out, multiplexer_2_out;

  _8_BitRegister _8_bitregister_1 (.I(multiplexer_1_out), .W(not_3_out), .R(1'b1), .O(_8_bitregister_1_o));
  Multiplexer #(.Bits(8)) multiplexer_1 (.sel(not_1_out), .in_0(JT), .in_1(multiplexer_2_out), .out(multiplexer_1_out));
  not not_1 (not_1_out, _8bitin1bit_1_out);
  _8BitIn1Bit _8bitin1bit_1 (.in(JT), .out(_8bitin1bit_1_out));
  _8BitIn1Bit _8bitin1bit_2 (.in(JT), .out(_8bitin1bit_2_out));
  Multiplexer #(.Bits(8)) multiplexer_2 (
    .sel(not_2_out), .in_0({8{1'b0}}), .in_1(_8bitparalleladder_1_re), .out(multiplexer_2_out));
  not not_2 (not_2_out, R);
  or or_1 (or_1_out, _8bitin1bit_2_out, R);
  not not_3 (not_3_out, C);
  Multiplexer multiplexer_3 (.sel(or_1_out), .in_0(C), .in_1(1'b1), .out(multiplexer_3_out));
  _8BitParallelAdder _8bitparalleladder_1 (
    .X({8{1'b0}}), .Y(Add), .Ca_in(1'b1), .Ca_out(Ca), .re(_8bitparalleladder_1_re));
  RAMAsync #(.Bits(8)) ramasync_1 (.A(2'b01), .D(_8_bitregister_1_o), .we(multiplexer_3_out), .Q(Add));
endmodule
