// Digital circuit ControlUnit.dig as structural Verilog
module ControlUnit (
  input  [23:0] Decodierung,
  input  Ca,
  input  _0,
  input  in_21,
  input  RDY,
  input  clock,
  output MDR_inSplit,
  output MDR_outOP,
  output MAR_in,
  output WR,
  output RD,
  output IR_in,
  output IR_op_out,
  output IP_in,
  output IP_out,
  output R_in,
  output R_out,
  output [1:0] SR_eq_ROPx,
  output B_in,
  output Y_in,
  output Y_out,
  output A_in,
  output ALU_out,
  output [3:0] F_eq_x,
  output [7:0] IterationPoint,
  output MDR_outA0,
  output MDR_outA1,
  output MDR_out,
  output MDR_inBus
);

  wire _8bitin1bit_1_out, and_1_out, and_2_out, delay_1_out, kombinatorischeschaltung_1__0,
       kombinatorischeschaltung_1_ca, kombinatorischeschaltung_1_de, kombinatorischeschaltung_1_out_22,
       kombinatorischeschaltung_1_r, kombinatorischeschaltung_1_wrdy, multiplexer_2_out, multiplexer_3_out,
       multiplexer_4_out, or_1_out;
  wire [1:0] kombinatorischeschaltung_1_checkflag;
  wire [7:0] kombinatorischeschaltung_1_na, multiplexer_1_out;

  Multiplexer #(.Bits(8)) multiplexer_1 (
    .sel(kombinatorischeschaltung_1_de), .in_0(kombinatorischeschaltung_1_na), .in_1(Decodierung[7:0]),
    .out(multiplexer_1_out));
  _8BitIn1Bit _8bitin1bit_1 (.in(Decodierung[7:0]), .out(_8bitin1bit_1_out));
  and and_1 (and_1_out, RDY, clock);
  Multiplexer multiplexer_2 (.sel(delay_1_out), .in_0(clock), .in_1(and_1_out), .out(multiplexer_2_out));
  and and_2 (and_2_out, ~_8bitin1bit_1_out, kombinatorischeschaltung_1_de);  // And
  KombinatorischeSchaltung kombinatorischeschaltung_1 (
    .MDR_inBus(MDR_inBus), .MDR_inSplit(MDR_inSplit), .MDR_out(MDR_out), .MDR_outA1(MDR_outA1),
    .MDR_outA0(MDR_outA0), .MDR_outOP(MDR_outOP), .MAR_in(MAR_in), .IR_in(IR_in), .IR_op_out(IR_op_out),
    .IP_in(IP_in), .IP_out(IP_out), .R_in(R_in), .R_out(R_out), .SR_eq_ROPx(SR_eq_ROPx), .Y_in(Y_in),
    .Y_out(Y_out), .B_in(B_in), .A_in(A_in), .ALU_out(ALU_out), .F_eq_x(F_eq_x),
    .Ca(kombinatorischeschaltung_1_ca), ._0(kombinatorischeschaltung_1__0),
    .out_22(kombinatorischeschaltung_1_out_22), .CheckFlag(kombinatorischeschaltung_1_checkflag), .RD(RD),
    .WR(WR), .NA(kombinatorischeschaltung_1_na), .R(kombinatorischeschaltung_1_r),
    .De(kombinatorischeschaltung_1_de), .WRDY(kombinatorischeschaltung_1_wrdy), .S_equenz(IterationPoint));
  Multiplexer multiplexer_3 (.sel(and_2_out), .in_0(or_1_out), .in_1(1'b1), .out(multiplexer_3_out));
  Delay delay_1 (.in(kombinatorischeschaltung_1_wrdy), .out(delay_1_out));
  \_8BitSequenzenzähler  \_8bitsequenzenzähler_1  (
    .C(multiplexer_2_out), .JT(multiplexer_1_out), .R(multiplexer_3_out), .Add(IterationPoint));
  or or_1 (or_1_out, kombinatorischeschaltung_1_r, multiplexer_4_out);
  Multiplexer #(.Selector_Bits(2)) multiplexer_4 (
    .sel(kombinatorischeschaltung_1_checkflag), .in_0(1'b0), .in_1(Ca), .in_2(_0), .in_3(in_21),
    .out(multiplexer_4_out));
endmodule
