// Digital circuit DummyTest.dig as structural Verilog
module DummyTest (
  input  I,
  input  S,
  input  i_2,
  input  w,
  input  i2,
  input  w2,
  input  i3,
  input  w3,
  input  I_3,
  input  S_2,
  input  i4,
  input  w4,
  input  I_4,
  input  S_3,
  input  C,
  input  [7:0] JT,
  input  R,
  input  C_2,
  input  [7:0] JT_2,
  input  R_2,
  input  C_3,
  input  [7:0] JT_3,
  input  R_3,
  input  [7:0] I_5,
  input  W_2,
  input  R_4,
  input  [7:0] I_6,
  input  W_3,
  input  R_5,
  output O,
  output o_2,
  output o2,
  output o2_2,
  output o3,
  output o3_2,
  output O_3,
  output O4,
  output O_4,
  output [7:0] Add,
  output Ca,
  output [7:0] Add_2,
  output Ca_2,
  output [7:0] Add_3,
  output Ca_3,
  output [7:0] O_5,
  output [7:0] O_6
);

  wire _8bitin1bit_1_out, _8bitin1bit_2_out, _8bitin1bit_3_out, _8bitin1bit_4_out, _8bitin1bit_5_out,
       _8bitin1bit_6_out, and_1_out, and_2_out, and_3_out, and_4_out, and_5_out, and_6_out, and_7_out,
       and_8_out, and_9_out, and_10_out, and_11_out, and_12_out, and_13_out, and_14_out, and_15_out,
       and_16_out, and_17_out, and_18_out, and_20_out, and_21_out, multiplexer_1_out, multiplexer_2_out,
       multiplexer_3_out, multiplexer_8_out, multiplexer_13_out, nand_1_out, nand_2_out, nand_5_out,
       nand_6_out, nand_7_out, nand_8_out, not_1_out, not_2_out, not_3_out, not_4_out, not_5_out, not_6_out,
       not_7_out, not_8_out, not_9_out, not_10_out, not_11_out, not_12_out, not_13_out, not_14_out, or_1_out,
       or_2_out, or_4_out, or_5_out, xor_1_out, xor_2_out, xor_3_out;
  wire [7:0] _1_bitmemorywr_1_o, _1_bitmemorywr_9_o, _8_bitregister_1_o, _8_bitregister_2_o,
       _8_bitregister_5_o, _8bitparalleladder_1_re, _8bitparalleladder_2_re, _8bitparalleladder_3_re,
       delay_1_out, delay_2_out, multiplexer_4_out, multiplexer_5_out, multiplexer_6_out, multiplexer_7_out,
       multiplexer_10_out, multiplexer_11_out;

  not not_1 (not_1_out, S_3);
  and and_1 (and_1_out, not_1_out, I_4);
  not not_2 (not_2_out, S_2);
  and and_2 (and_2_out, not_2_out, I_3);
  not not_3 (not_3_out, S);
  and and_3 (and_3_out, not_3_out, I);
  xor xor_1 (xor_1_out, S_3, I_4);
  and and_4 (and_4_out, S_3, I_4);
  xor xor_2 (xor_2_out, S_2, I_3);
  and and_5 (and_5_out, S_2, I_3);
  Multiplexer multiplexer_1 (.sel(xor_1_out), .in_0(1'b0), .in_1(I_4), .out(multiplexer_1_out));
  xor xor_3 (xor_3_out, S, I);
  and and_6 (and_6_out, S, I);
  _8BitIn1Bit _8bitin1bit_1 (.in(JT_2), .out(_8bitin1bit_1_out));
  and and_7 (and_7_out, and_1_out, 1'b1);
  and and_8 (and_8_out, 1'b1, and_4_out);
  Multiplexer multiplexer_2 (.sel(xor_2_out), .in_0(1'b0), .in_1(I_3), .out(multiplexer_2_out));
  Multiplexer multiplexer_3 (.sel(xor_3_out), .in_0(1'b0), .in_1(I), .out(multiplexer_3_out));
  _8_BitRegister _8_bitregister_1 (.I(_8bitparalleladder_1_re), .W(not_9_out), .R(1'b1), .O(_8_bitregister_1_o));
  Multiplexer #(.Bits(8)) multiplexer_4 (
    .sel(_8bitin1bit_1_out), .in_0(_8_bitregister_1_o), .in_1(JT_2), .out(multiplexer_4_out));
  _8_BitRegister _8_bitregister_2 (.I(multiplexer_7_out), .W(not_7_out), .R(1'b1), .O(_8_bitregister_2_o));
  _8BitIn1Bit _8bitin1bit_2 (.in(JT), .out(_8bitin1bit_2_out));
  not not_4 (not_4_out, and_8_out);
  and and_9 (and_9_out, and_2_out, 1'b1);
  and and_10 (and_10_out, 1'b1, and_5_out);
  and and_11 (and_11_out, and_3_out, 1'b1);
  and and_12 (and_12_out, 1'b1, and_6_out);
  Multiplexer #(.Bits(8)) multiplexer_5 (
    .sel(_8bitin1bit_2_out), .in_0(_8_bitregister_2_o), .in_1(JT), .out(multiplexer_5_out));
  not not_5 (not_5_out, and_10_out);
  not not_6 (not_6_out, and_12_out);
  and and_13 (and_13_out, i_2, w);
  and and_14 (and_14_out, ~i_2, w);  // And
  Multiplexer #(.Bits(8)) multiplexer_6 (
    .sel(R_2), .in_0(multiplexer_4_out), .in_1({8{1'b0}}), .out(multiplexer_6_out));
  Multiplexer #(.Bits(8)) multiplexer_7 (
    .sel(not_8_out), .in_0({8{1'b0}}), .in_1(_8bitparalleladder_2_re), .out(multiplexer_7_out));
  not not_7 (not_7_out, C);
  not not_8 (not_8_out, R);
  nand nand_1 (nand_1_out, i2, w2);
  nand nand_2 (nand_2_out, ~i2, w2);  // NAnd
  not not_9 (not_9_out, C_2);
  Multiplexer multiplexer_8 (.sel(R), .in_0(C), .in_1(1'b1), .out(multiplexer_8_out));
  or or_1 (or_1_out, o_2, and_13_out);
  _8_BitRegister _8_bitregister_3 (.I(multiplexer_6_out), .W(C_2), .R(1'b1), .O(Add_2));
  _8_BitRegister _8_bitregister_4 (.I(multiplexer_5_out), .W(multiplexer_8_out), .R(1'b1), .O(Add));
  _8BitParallelAdder _8bitparalleladder_1 (
    .X({8{1'b0}}), .Y(Add_2), .Ca_in(1'b1), .Ca_out(Ca_2), .re(_8bitparalleladder_1_re));
  _8BitParallelAdder _8bitparalleladder_2 (
    .X({8{1'b0}}), .Y(Add), .Ca_in(1'b1), .Ca_out(Ca), .re(_8bitparalleladder_2_re));
  or or_2 (or_2_out, multiplexer_1_out, and_15_out);
  and and_15 (and_15_out, or_2_out, ~and_7_out);  // And
  and and_16 (and_16_out, multiplexer_3_out, and_11_out);
  and and_17 (and_17_out, ~multiplexer_3_out, and_11_out);  // And
  nand nand_3 (o2, nand_1_out, o2_2);
  nand nand_4 (o2_2, o2, nand_2_out);
  nor nor_1 (o3_2, i3, o3);
  nor nor_2 (o3, o3_2, w3);
  or or_3 (O4, i4, and_18_out);
  and and_18 (and_18_out, O4, ~w4);  // And
  nand nand_5 (nand_5_out, multiplexer_2_out, and_9_out);
  nand nand_6 (nand_6_out, ~multiplexer_2_out, and_9_out);  // NAnd
  or or_4 (or_4_out, and_20_out, and_16_out);
  and and_19 (o_2, or_1_out, ~and_14_out);  // And
  and and_20 (and_20_out, or_4_out, ~and_17_out);  // And
  nand nand_7 (nand_7_out, nand_5_out, nand_8_out);
  nand nand_8 (nand_8_out, nand_7_out, nand_6_out);
  Multiplexer multiplexer_9 (.sel(not_6_out), .in_0(and_20_out), .in_1(1'b0), .out(O));
  _8_BitRegister _8_bitregister_5 (.I(multiplexer_10_out), .W(not_12_out), .R(1'b1), .O(_8_bitregister_5_o));
  Multiplexer #(.Bits(8)) multiplexer_10 (
    .sel(not_10_out), .in_0(JT_3), .in_1(multiplexer_11_out), .out(multiplexer_10_out));
  not not_10 (not_10_out, _8bitin1bit_3_out);
  _8BitIn1Bit _8bitin1bit_3 (.in(JT_3), .out(_8bitin1bit_3_out));
  _8BitIn1Bit _8bitin1bit_4 (.in(JT_3), .out(_8bitin1bit_4_out));
  not not_11 (not_11_out, R_3);
  Multiplexer #(.Bits(8)) multiplexer_11 (
    .sel(not_11_out), .in_0({8{1'b0}}), .in_1(_8bitparalleladder_3_re), .out(multiplexer_11_out));
  not not_12 (not_12_out, C_3);
  or or_5 (or_5_out, _8bitin1bit_4_out, R_3);
  Multiplexer multiplexer_12 (.sel(not_4_out), .in_0(or_2_out), .in_1(1'b0), .out(O_4));
  Multiplexer multiplexer_13 (.sel(or_5_out), .in_0(C_3), .in_1(1'b1), .out(multiplexer_13_out));
  Multiplexer multiplexer_14 (.sel(not_5_out), .in_0(nand_7_out), .in_1(1'b0), .out(O_3));
  _8_BitRegister _8_bitregister_6 (.I(_8_bitregister_5_o), .W(multiplexer_13_out), .R(1'b1), .O(Add_3));
  _8BitParallelAdder _8bitparalleladder_3 (
    .X({8{1'b0}}), .Y(Add_3), .Ca_in(1'b1), .Ca_out(Ca_3), .re(_8bitparalleladder_3_re));
  _8BitIn1Bit _8bitin1bit_5 (.in(_1_bitmemorywr_1_o), .out(_8bitin1bit_5_out));
  Multiplexer #(.Bits(8)) multiplexer_15 (.sel(not_13_out), .in_0(delay_1_out), .in_1(I_5), .out(O_5));
  Delay #(.Bits(8), .delayTime(2)) delay_1 (.in(_1_bitmemorywr_1_o), .out(delay_1_out));
  _1_BitMemoryWR _1_bitmemorywr_1 (.o(_1_bitmemorywr_1_o[0]), .i(I_5[0]), .y(1'b1), .w(W_2), .r(R_4), .x(1'b1));
  _1_BitMemoryWR _1_bitmemorywr_2 (.o(_1_bitmemorywr_1_o[1]), .i(I_5[1]), .y(1'b1), .w(W_2), .r(R_4), .x(1'b1));
  _1_BitMemoryWR _1_bitmemorywr_3 (.o(_1_bitmemorywr_1_o[2]), .i(I_5[2]), .y(1'b1), .w(W_2), .r(R_4), .x(1'b1));
  _1_BitMemoryWR _1_bitmemorywr_4 (.o(_1_bitmemorywr_1_o[3]), .i(I_5[3]), .y(1'b1), .w(W_2), .r(R_4), .x(1'b1));
  _1_BitMemoryWR _1_bitmemorywr_5 (.o(_1_bitmemorywr_1_o[4]), .i(I_5[4]), .y(1'b1), .w(W_2), .r(R_4), .x(1'b1));
  _1_BitMemoryWR _1_bitmemorywr_6 (.o(_1_bitmemorywr_1_o[5]), .i(I_5[5]), .y(1'b1), .w(W_2), .r(R_4), .x(1'b1));
  _1_BitMemoryWR _1_bitmemorywr_7 (.o(_1_bitmemorywr_1_o[6]), .i(I_5[6]), .y(1'b1), .w(W_2), .r(R_4), .x(1'b1));
  _1_BitMemoryWR _1_bitmemorywr_8 (.o(_1_bitmemorywr_1_o[7]), .i(I_5[7]), .y(1'b1), .w(W_2), .r(R_4), .x(1'b1));
  not not_13 (not_13_out, _8bitin1bit_5_out);
  _8BitIn1Bit _8bitin1bit_6 (.in(_1_bitmemorywr_9_o), .out(_8bitin1bit_6_out));
  Multiplexer #(.Bits(8)) multiplexer_16 (.sel(and_21_out), .in_0(delay_2_out), .in_1(I_6), .out(O_6));
  Delay #(.Bits(8), .delayTime(2)) delay_2 (.in(_1_bitmemorywr_9_o), .out(delay_2_out));
  _1_BitMemoryWR _1_bitmemorywr_9 (.o(_1_bitmemorywr_9_o[0]), .i(I_6[0]), .y(1'b1), .w(W_3), .r(R_5), .x(1'b1));
  _1_BitMemoryWR _1_bitmemorywr_10 (.o(_1_bitmemorywr_9_o[1]), .i(I_6[1]), .y(1'b1), .w(W_3), .r(R_5), .x(1'b1));
  _1_BitMemoryWR _1_bitmemorywr_11 (.o(_1_bitmemorywr_9_o[2]), .i(I_6[2]), .y(1'b1), .w(W_3), .r(R_5), .x(1'b1));
  _1_BitMemoryWR _1_bitmemorywr_12 (.o(_1_bitmemorywr_9_o[3]), .i(I_6[3]), .y(1'b1), .w(W_3), .r(R_5), .x(1'b1));
  _1_BitMemoryWR _1_bitmemorywr_13 (.o(_1_bitmemorywr_9_o[4]), .i(I_6[4]), .y(1'b1), .w(W_3), .r(R_5), .x(1'b1));
  _1_BitMemoryWR _1_bitmemorywr_14 (.o(_1_bitmemorywr_9_o[5]), .i(I_6[5]), .y(1'b1), .w(W_3), .r(R_5), .x(1'b1));
  _1_BitMemoryWR _1_bitmemorywr_15 (.o(_1_bitmemorywr_9_o[6]), .i(I_6[6]), .y(1'b1), .w(W_3), .r(R_5), .x(1'b1));
  _1_BitMemoryWR _1_bitmemorywr_16 (.o(_1_bitmemorywr_9_o[7]), .i(I_6[7]), .y(1'b1), .w(W_3), .r(R_5), .x(1'b1));
  not not_14 (not_14_out, _8bitin1bit_6_out);
  and and_21 (and_21_out, W_3, R_5, not_14_out);

  // Notes on the sheet:
  //   D_type FlipFlop -> Random begin Output
  //   RS-FlipFlop
  //   RS-FlipFlop no random anfang
endmodule
