// Digital circuit 24BitCalc.dig as structural Verilog
module _24BitCalc (
  input  [23:0] x,
  input  [23:0] y,
  input  plus,
  input  Ca_in,
  output [23:0] Re,
  output Ca_out
);

  wire _24bitparalleladder_1_ca_out, multiplexer_1_out, multiplexer_3_out, not_1_out;
  wire [23:0] _24bitnegation_1_o, _24bitparalleladder_1_re, multiplexer_2_out;

  _24BitParallelAdder _24bitparalleladder_1 (
    .X(24'h1), .Y(y), .Ca_in(1'b0), .Ca_out(_24bitparalleladder_1_ca_out), .re(_24bitparalleladder_1_re));
  LED led_1 (.in(_24bitparalleladder_1_ca_out));
  Multiplexer multiplexer_1 (.sel(plus), .in_0(1'b0), .in_1(Ca_in), .out(multiplexer_1_out));
  not not_1 (not_1_out, multiplexer_1_out);
  Multiplexer #(.Bits(24)) multiplexer_2 (
    .sel(not_1_out), .in_0(_24bitparalleladder_1_re), .in_1(y), .out(multiplexer_2_out));
  Multiplexer multiplexer_3 (.sel(plus), .in_0(Ca_in), .in_1(1'b0), .out(multiplexer_3_out));
  _24BitNegation _24bitnegation_1 (.Enable(plus), .i(multiplexer_2_out), .o(_24bitnegation_1_o));
  _24BitParallelAdder _24bitparalleladder_2 (
    .X(x), .Y(_24bitnegation_1_o), .Ca_in(multiplexer_3_out), .Ca_out(Ca_out), .re(Re));
endmodule
