// Digital circuit 24BitNegation.dig as structural Verilog
module _24BitNegation (
  input  Enable,
  input  [23:0] i,
  output [23:0] o
);

  wire _12bitparalleladder_1_ca_out;
  wire [11:0] xor_9_out, xor_13_out;

  xor xor_1 (xor_9_out[11], i[23], Enable);
  xor xor_2 (xor_9_out[10], i[22], Enable);
  xor xor_3 (xor_9_out[9], i[21], Enable);
  xor xor_4 (xor_9_out[8], i[20], Enable);
  xor xor_5 (xor_9_out[7], i[19], Enable);
  xor xor_6 (xor_9_out[6], i[18], Enable);
  xor xor_7 (xor_9_out[5], i[17], Enable);
  xor xor_8 (xor_9_out[4], i[16], Enable);
  xor xor_9 (xor_9_out[3], i[15], Enable);
  xor xor_10 (xor_9_out[2], i[14], Enable);
  xor xor_11 (xor_9_out[1], i[13], Enable);
  xor xor_12 (xor_9_out[0], i[12], Enable);
  xor xor_13 (xor_13_out[11], i[11], Enable);
  xor xor_14 (xor_13_out[10], i[10], Enable);
  xor xor_15 (xor_13_out[9], i[9], Enable);
  xor xor_16 (xor_13_out[8], i[8], Enable);
  xor xor_17 (xor_13_out[7], i[7], Enable);
  xor xor_18 (xor_13_out[6], i[6], Enable);
  xor xor_19 (xor_13_out[5], i[5], Enable);
  xor xor_20 (xor_13_out[4], i[4], Enable);
  xor xor_21 (xor_13_out[3], i[3], Enable);
  xor xor_22 (xor_13_out[2], i[2], Enable);
  xor xor_23 (xor_13_out[1], i[1], Enable);
  xor xor_24 (xor_13_out[0], i[0], Enable);
  _12BitParallelAdder _12bitparalleladder_1 (
    .X(xor_13_out), .Y({12{1'b0}}), .Ca_in(Enable), .Ca_out(_12bitparalleladder_1_ca_out), .re(o[11:0]));
  _12BitParallelAdder _12bitparalleladder_2 (
    .X({12{1'b0}}), .Y(xor_9_out), .Ca_in(_12bitparalleladder_1_ca_out), .re(o[23:12]));  // open: Ca_out
endmodule
