// Digital circuit 12BitParallelAdder.dig as structural Verilog
module _12BitParallelAdder (
  input  [11:0] X,
  input  [11:0] Y,
  input  Ca_in,
  output Ca_out,
  output [11:0] re
);

  wire volladdierer_1_ca_out, volladdierer_2_ca_out, volladdierer_3_ca_out, volladdierer_4_ca_out,
       volladdierer_5_ca_out, volladdierer_6_ca_out, volladdierer_7_ca_out, volladdierer_8_ca_out,
       volladdierer_9_ca_out, volladdierer_10_ca_out, volladdierer_11_ca_out;

  VollAddierer volladdierer_1 (.ca_in(Ca_in), .x(X[0]), .y(Y[0]), .re(re[0]), .ca_out(volladdierer_1_ca_out));
  VollAddierer volladdierer_2 (
    .ca_in(volladdierer_1_ca_out), .x(X[1]), .y(Y[1]), .re(re[1]), .ca_out(volladdierer_2_ca_out));
  VollAddierer volladdierer_3 (
    .ca_in(volladdierer_2_ca_out), .x(X[2]), .y(Y[2]), .re(re[2]), .ca_out(volladdierer_3_ca_out));
  VollAddierer volladdierer_4 (
    .ca_in(volladdierer_3_ca_out), .x(X[3]), .y(Y[3]), .re(re[3]), .ca_out(volladdierer_4_ca_out));
  VollAddierer volladdierer_5 (
    .ca_in(volladdierer_4_ca_out), .x(X[4]), .y(Y[4]), .re(re[4]), .ca_out(volladdierer_5_ca_out));
  VollAddierer volladdierer_6 (
    .ca_in(volladdierer_5_ca_out), .x(X[5]), .y(Y[5]), .re(re[5]), .ca_out(volladdierer_6_ca_out));
  VollAddierer volladdierer_7 (
    .ca_in(volladdierer_6_ca_out), .x(X[6]), .y(Y[6]), .re(re[6]), .ca_out(volladdierer_7_ca_out));
  VollAddierer volladdierer_8 (
    .ca_in(volladdierer_7_ca_out), .x(X[7]), .y(Y[7]), .re(re[7]), .ca_out(volladdierer_8_ca_out));
  VollAddierer volladdierer_9 (
    .ca_in(volladdierer_8_ca_out), .x(X[8]), .y(Y[8]), .re(re[8]), .ca_out(volladdierer_9_ca_out));
  VollAddierer volladdierer_10 (
    .ca_in(volladdierer_9_ca_out), .x(X[9]), .y(Y[9]), .re(re[9]), .ca_out(volladdierer_10_ca_out));
  VollAddierer volladdierer_11 (
    .ca_in(volladdierer_10_ca_out), .x(X[10]), .y(Y[10]), .re(re[10]), .ca_out(volladdierer_11_ca_out));
  VollAddierer volladdierer_12 (.ca_in(volladdierer_11_ca_out), .x(X[11]), .y(Y[11]), .re(re[11]), .ca_out(Ca_out));
endmodule
