// Digital circuit 24BitParallelAdder.dig as structural Verilog
module _24BitParallelAdder (
  input  [23:0] X,
  input  [23:0] Y,
  input  Ca_in,
  output Ca_out,
  output [23:0] re
);

  wire volladdierer_1_ca_out, volladdierer_2_ca_out, volladdierer_3_ca_out, volladdierer_4_ca_out,
       volladdierer_5_ca_out, volladdierer_6_ca_out, volladdierer_7_ca_out, volladdierer_8_ca_out,
       volladdierer_9_ca_out, volladdierer_10_ca_out, volladdierer_11_ca_out, volladdierer_12_ca_out,
       volladdierer_13_ca_out, volladdierer_14_ca_out, volladdierer_15_ca_out, volladdierer_16_ca_out,
       volladdierer_17_ca_out, volladdierer_18_ca_out, volladdierer_19_ca_out, volladdierer_20_ca_out,
       volladdierer_21_ca_out, volladdierer_22_ca_out, volladdierer_23_ca_out;

  VollAddierer volladdierer_1 (.ca_in(Ca_in), .x(X[0]), .y(Y[0]), .re(re[0]), .ca_out(volladdierer_1_ca_out));
  VollAddierer volladdierer_2 (
    .ca_in(volladdierer_1_ca_out), .x(X[1]), .y(Y[1]), .re(re[1]), .ca_out(volladdierer_2_ca_out));
  VollAddierer volladdierer_3 (
    .ca_in(volladdierer_2_ca_out), .x(X[2]), .y(Y[2]), .re(re[2]), .ca_out(volladdierer_3_ca_out));
  VollAddierer volladdierer_4 (
    .ca_in(volladdierer_3_ca_out), .x(X[3]), .y(Y[3]), .re(re[3]), .ca_out(volladdierer_4_ca_out));
  VollAddierer volladdierer_5 (
    .ca_in(volladdierer_4_ca_out), .x(X[4]), .y(Y[4]), .re(re[4]), .ca_out(volladdierer_5_ca_out));
  VollAddierer volladdierer_6 (
    .ca_in(volladdierer_5_ca_out), .x(X[5]), .y(Y[5]), .re(re[5]), .ca_out(volladdierer_6_ca_out));
  VollAddierer volladdierer_7 (
    .ca_in(volladdierer_6_ca_out), .x(X[6]), .y(Y[6]), .re(re[6]), .ca_out(volladdierer_7_ca_out));
  VollAddierer volladdierer_8 (
    .ca_in(volladdierer_7_ca_out), .x(X[7]), .y(Y[7]), .re(re[7]), .ca_out(volladdierer_8_ca_out));
  VollAddierer volladdierer_9 (
    .ca_in(volladdierer_8_ca_out), .x(X[8]), .y(Y[8]), .re(re[8]), .ca_out(volladdierer_9_ca_out));
  VollAddierer volladdierer_10 (
    .ca_in(volladdierer_9_ca_out), .x(X[9]), .y(Y[9]), .re(re[9]), .ca_out(volladdierer_10_ca_out));
  VollAddierer volladdierer_11 (
    .ca_in(volladdierer_10_ca_out), .x(X[10]), .y(Y[10]), .re(re[10]), .ca_out(volladdierer_11_ca_out));
  VollAddierer volladdierer_12 (
    .ca_in(volladdierer_11_ca_out), .x(X[11]), .y(Y[11]), .re(re[11]), .ca_out(volladdierer_12_ca_out));
  VollAddierer volladdierer_13 (
    .ca_in(volladdierer_12_ca_out), .x(X[12]), .y(Y[12]), .re(re[12]), .ca_out(volladdierer_13_ca_out));
  VollAddierer volladdierer_14 (
    .ca_in(volladdierer_13_ca_out), .x(X[13]), .y(Y[13]), .re(re[13]), .ca_out(volladdierer_14_ca_out));
  VollAddierer volladdierer_15 (
    .ca_in(volladdierer_14_ca_out), .x(X[14]), .y(Y[14]), .re(re[14]), .ca_out(volladdierer_15_ca_out));
  VollAddierer volladdierer_16 (
    .ca_in(volladdierer_15_ca_out), .x(X[15]), .y(Y[15]), .re(re[15]), .ca_out(volladdierer_16_ca_out));
  VollAddierer volladdierer_17 (
    .ca_in(volladdierer_16_ca_out), .x(X[16]), .y(Y[16]), .re(re[16]), .ca_out(volladdierer_17_ca_out));
  VollAddierer volladdierer_18 (
    .ca_in(volladdierer_17_ca_out), .x(X[17]), .y(Y[17]), .re(re[17]), .ca_out(volladdierer_18_ca_out));
  VollAddierer volladdierer_19 (
    .ca_in(volladdierer_18_ca_out), .x(X[18]), .y(Y[18]), .re(re[18]), .ca_out(volladdierer_19_ca_out));
  VollAddierer volladdierer_20 (
    .ca_in(volladdierer_19_ca_out), .x(X[19]), .y(Y[19]), .re(re[19]), .ca_out(volladdierer_20_ca_out));
  VollAddierer volladdierer_21 (
    .ca_in(volladdierer_20_ca_out), .x(X[20]), .y(Y[20]), .re(re[20]), .ca_out(volladdierer_21_ca_out));
  VollAddierer volladdierer_22 (
    .ca_in(volladdierer_21_ca_out), .x(X[21]), .y(Y[21]), .re(re[21]), .ca_out(volladdierer_22_ca_out));
  VollAddierer volladdierer_23 (
    .ca_in(volladdierer_22_ca_out), .x(X[22]), .y(Y[22]), .re(re[22]), .ca_out(volladdierer_23_ca_out));
  VollAddierer volladdierer_24 (.ca_in(volladdierer_23_ca_out), .x(X[23]), .y(Y[23]), .re(re[23]), .ca_out(Ca_out));
endmodule
