// Digital circuit VollAddierer.dig as structural Verilog
module VollAddierer (
  input  ca_in,
  input  x,
  input  y,
  output re,
  output ca_out
);

  wire halbaddierer_1_c, halbaddierer_1_e, halbaddierer_2_c;

  halbAddierer halbaddierer_1 (.a(x), .b(y), .E(halbaddierer_1_e), .C(halbaddierer_1_c));
  halbAddierer halbaddierer_2 (.a(ca_in), .b(halbaddierer_1_e), .E(re), .C(halbaddierer_2_c));
  or or_1 (ca_out, halbaddierer_2_c, halbaddierer_1_c);
endmodule
