// Digital circuit halbAddierer.dig as structural Verilog
module halbAddierer (
  input  a,
  input  b,
  output E,
  output C
);

  wire and_1_out, not_1_out;

  xor xor_1 (E, a, b);
  and and_1 (and_1_out, b, a);
  not not_1 (not_1_out, E);
  and and_2 (C, not_1_out, and_1_out);
endmodule
