// Digital circuit 24BitEnd.dig as structural Verilog
module _24BitEnd (
  input  [23:0] i
);

  LED led_1 (.in(i[0]));
  LED led_2 (.in(i[1]));
  LED led_3 (.in(i[2]));
  LED led_4 (.in(i[3]));
  LED led_5 (.in(i[4]));
  LED led_6 (.in(i[5]));
  LED led_7 (.in(i[6]));
  LED led_8 (.in(i[7]));
  LED led_9 (.in(i[8]));
  LED led_10 (.in(i[9]));
  LED led_11 (.in(i[10]));
  LED led_12 (.in(i[11]));
  LED led_13 (.in(i[12]));
  LED led_14 (.in(i[13]));
  LED led_15 (.in(i[14]));
  LED led_16 (.in(i[15]));
  LED led_17 (.in(i[16]));
  LED led_18 (.in(i[17]));
  LED led_19 (.in(i[18]));
  LED led_20 (.in(i[19]));
  LED led_21 (.in(i[20]));
  LED led_22 (.in(i[21]));
  LED led_23 (.in(i[22]));
  LED led_24 (.in(i[23]));
endmodule
