// Digital circuit 24BitIn1Bit.dig as structural Verilog
module _24BitIn1Bit (
  input  [23:0] in,
  output out
);

  or or_1 (out, in[0], in[1], in[2], in[3], in[4], in[5], in[6], in[7], in[8], in[9], in[10], in[11], in[12], in[13], in[14], in[15], in[16], in[17], in[18], in[19], in[20], in[21], in[22], in[23]);
endmodule
