// Digital circuit 24BitIsEqual.dig as structural Verilog
module _24BitIsEqual (
  input  [23:0] i_0,
  input  [23:0] i_1,
  output isEqual
);

  wire xnor_1_out, xnor_2_out, xnor_3_out, xnor_4_out, xnor_5_out, xnor_6_out, xnor_7_out, xnor_8_out,
       xnor_9_out, xnor_10_out, xnor_11_out, xnor_12_out, xnor_13_out, xnor_14_out, xnor_15_out, xnor_16_out,
       xnor_17_out, xnor_18_out, xnor_19_out, xnor_20_out, xnor_21_out, xnor_22_out, xnor_23_out, xnor_24_out;

  xnor xnor_1 (xnor_1_out, i_1[0], i_0[0]);
  xnor xnor_2 (xnor_2_out, i_1[1], i_0[1]);
  xnor xnor_3 (xnor_3_out, i_1[2], i_0[2]);
  xnor xnor_4 (xnor_4_out, i_1[3], i_0[3]);
  xnor xnor_5 (xnor_5_out, i_1[4], i_0[4]);
  xnor xnor_6 (xnor_6_out, i_1[5], i_0[5]);
  xnor xnor_7 (xnor_7_out, i_1[6], i_0[6]);
  and and_1 (isEqual, xnor_1_out, xnor_2_out, xnor_3_out, xnor_4_out, xnor_5_out, xnor_6_out, xnor_7_out, xnor_8_out, xnor_9_out, xnor_10_out, xnor_11_out, xnor_12_out, xnor_13_out, xnor_14_out, xnor_15_out, xnor_16_out, xnor_17_out, xnor_18_out, xnor_19_out, xnor_20_out, xnor_21_out, xnor_22_out, xnor_23_out, xnor_24_out);
  xnor xnor_8 (xnor_8_out, i_1[7], i_0[7]);
  xnor xnor_9 (xnor_9_out, i_1[8], i_0[8]);
  xnor xnor_10 (xnor_10_out, i_1[9], i_0[9]);
  xnor xnor_11 (xnor_11_out, i_1[10], i_0[10]);
  xnor xnor_12 (xnor_12_out, i_1[11], i_0[11]);
  xnor xnor_13 (xnor_13_out, i_1[12], i_0[12]);
  xnor xnor_14 (xnor_14_out, i_1[13], i_0[13]);
  xnor xnor_15 (xnor_15_out, i_1[14], i_0[14]);
  xnor xnor_16 (xnor_16_out, i_1[15], i_0[15]);
  xnor xnor_17 (xnor_17_out, i_1[16], i_0[16]);
  xnor xnor_18 (xnor_18_out, i_1[17], i_0[17]);
  xnor xnor_19 (xnor_19_out, i_1[18], i_0[18]);
  xnor xnor_20 (xnor_20_out, i_1[19], i_0[19]);
  xnor xnor_21 (xnor_21_out, i_1[20], i_0[20]);
  xnor xnor_22 (xnor_22_out, i_1[21], i_0[21]);
  xnor xnor_23 (xnor_23_out, i_1[22], i_0[22]);
  xnor xnor_24 (xnor_24_out, i_1[23], i_0[23]);
endmodule
