// Digital circuit 24BitIsNegativ.dig as structural Verilog
module _24BitIsNegativ (
  input  [23:0] I,
  output IsNeg
);

  _24BitEnd _24bitend_1 (.i({1'b1, I[22:0]}));

  assign IsNeg = I[23];
endmodule
