// Digital circuit 1-BitMemoryW.dig as structural Verilog
module _1_BitMemoryW (
  input  i,
  input  w,
  output o
);

  wire and_1_out, and_2_out, or_1_out;

  and and_1 (and_1_out, i, w);
  and and_2 (and_2_out, ~i, w);  // And
  or or_1 (or_1_out, o, and_1_out);
  and and_3 (o, or_1_out, ~and_2_out);  // And
endmodule
