// Digital circuit 1-BitMemoryWR.dig as structural Verilog
module _1_BitMemoryWR (
  input  i,
  input  w,
  input  r,
  input  x,
  input  y,
  output o
);

  wire _1_bitmemoryw_1_o, and_1_out, and_2_out, and_3_out, not_1_out;

  and and_1 (and_1_out, x, y);
  and and_2 (and_2_out, w, and_1_out);
  and and_3 (and_3_out, and_1_out, r);
  not not_1 (not_1_out, and_3_out);
  _1_BitMemoryW _1_bitmemoryw_1 (.i(i), .w(and_2_out), .o(_1_bitmemoryw_1_o));
  Multiplexer multiplexer_1 (.sel(not_1_out), .in_0(_1_bitmemoryw_1_o), .in_1(1'b0), .out(o));
endmodule
