// Digital circuit 24-BitRegister.dig as structural Verilog
module _24_BitRegister (
  input  [23:0] I,
  input  W,
  input  R,
  output [23:0] O
);

  wire _24bitin1bit_1_out, and_1_out, not_1_out;
  wire [23:0] _1_bitmemorywr_1_o, delay_1_out;

  Delay #(.Bits(24), .delayTime(3)) delay_1 (.in(_1_bitmemorywr_1_o), .out(delay_1_out));
  _24BitIn1Bit _24bitin1bit_1 (.in(_1_bitmemorywr_1_o), .out(_24bitin1bit_1_out));
  Multiplexer #(.Bits(24)) multiplexer_1 (.sel(and_1_out), .in_0(delay_1_out), .in_1(I), .out(O));
  not not_1 (not_1_out, _24bitin1bit_1_out);
  and and_1 (and_1_out, W, R, not_1_out);
  _1_BitMemoryWR _1_bitmemorywr_1 (.o(_1_bitmemorywr_1_o[0]), .i(I[0]), .y(1'b1), .w(W), .r(R), .x(1'b1));
  _1_BitMemoryWR _1_bitmemorywr_2 (.o(_1_bitmemorywr_1_o[1]), .i(I[1]), .y(1'b1), .w(W), .r(R), .x(1'b1));
  _1_BitMemoryWR _1_bitmemorywr_3 (.o(_1_bitmemorywr_1_o[2]), .i(I[2]), .y(1'b1), .w(W), .r(R), .x(1'b1));
  _1_BitMemoryWR _1_bitmemorywr_4 (.o(_1_bitmemorywr_1_o[3]), .i(I[3]), .y(1'b1), .w(W), .r(R), .x(1'b1));
  _1_BitMemoryWR _1_bitmemorywr_5 (.o(_1_bitmemorywr_1_o[4]), .i(I[4]), .y(1'b1), .w(W), .r(R), .x(1'b1));
  _1_BitMemoryWR _1_bitmemorywr_6 (.o(_1_bitmemorywr_1_o[5]), .i(I[5]), .y(1'b1), .w(W), .r(R), .x(1'b1));
  _1_BitMemoryWR _1_bitmemorywr_7 (.o(_1_bitmemorywr_1_o[6]), .i(I[6]), .y(1'b1), .w(W), .r(R), .x(1'b1));
  _1_BitMemoryWR _1_bitmemorywr_8 (.o(_1_bitmemorywr_1_o[7]), .i(I[7]), .y(1'b1), .w(W), .r(R), .x(1'b1));
  _1_BitMemoryWR _1_bitmemorywr_9 (.o(_1_bitmemorywr_1_o[8]), .i(I[8]), .y(1'b1), .w(W), .r(R), .x(1'b1));
  _1_BitMemoryWR _1_bitmemorywr_10 (.o(_1_bitmemorywr_1_o[9]), .i(I[9]), .y(1'b1), .w(W), .r(R), .x(1'b1));
  _1_BitMemoryWR _1_bitmemorywr_11 (.o(_1_bitmemorywr_1_o[10]), .i(I[10]), .y(1'b1), .w(W), .r(R), .x(1'b1));
  _1_BitMemoryWR _1_bitmemorywr_12 (.o(_1_bitmemorywr_1_o[11]), .i(I[11]), .y(1'b1), .w(W), .r(R), .x(1'b1));
  _1_BitMemoryWR _1_bitmemorywr_13 (.o(_1_bitmemorywr_1_o[12]), .i(I[12]), .y(1'b1), .w(W), .r(R), .x(1'b1));
  _1_BitMemoryWR _1_bitmemorywr_14 (.o(_1_bitmemorywr_1_o[13]), .i(I[13]), .y(1'b1), .w(W), .r(R), .x(1'b1));
  _1_BitMemoryWR _1_bitmemorywr_15 (.o(_1_bitmemorywr_1_o[14]), .i(I[14]), .y(1'b1), .w(W), .r(R), .x(1'b1));
  _1_BitMemoryWR _1_bitmemorywr_16 (.o(_1_bitmemorywr_1_o[15]), .i(I[15]), .y(1'b1), .w(W), .r(R), .x(1'b1));
  _1_BitMemoryWR _1_bitmemorywr_17 (.o(_1_bitmemorywr_1_o[16]), .i(I[16]), .y(1'b1), .w(W), .r(R), .x(1'b1));
  _1_BitMemoryWR _1_bitmemorywr_18 (.o(_1_bitmemorywr_1_o[17]), .i(I[17]), .y(1'b1), .w(W), .r(R), .x(1'b1));
  _1_BitMemoryWR _1_bitmemorywr_19 (.o(_1_bitmemorywr_1_o[18]), .i(I[18]), .y(1'b1), .w(W), .r(R), .x(1'b1));
  _1_BitMemoryWR _1_bitmemorywr_20 (.o(_1_bitmemorywr_1_o[19]), .i(I[19]), .y(1'b1), .w(W), .r(R), .x(1'b1));
  _1_BitMemoryWR _1_bitmemorywr_21 (.o(_1_bitmemorywr_1_o[20]), .i(I[20]), .y(1'b1), .w(W), .r(R), .x(1'b1));
  _1_BitMemoryWR _1_bitmemorywr_22 (.o(_1_bitmemorywr_1_o[21]), .i(I[21]), .y(1'b1), .w(W), .r(R), .x(1'b1));
  _1_BitMemoryWR _1_bitmemorywr_23 (.o(_1_bitmemorywr_1_o[22]), .i(I[22]), .y(1'b1), .w(W), .r(R), .x(1'b1));
  _1_BitMemoryWR _1_bitmemorywr_24 (.o(_1_bitmemorywr_1_o[23]), .i(I[23]), .y(1'b1), .w(W), .r(R), .x(1'b1));
endmodule
