// Digital circuit 736ByteRam.dig as structural Verilog
module _736ByteRam (
  input  [7:0] Add,
  input  W,
  input  R,
  input  [23:0] I,
  output [23:0] O
);

  _256BitMemory _0 (.Add(Add), .I(I[0]), .W(W), .R(R), .O(O[0]));
  _256BitMemory _1 (.Add(Add), .I(I[1]), .W(W), .R(R), .O(O[1]));
  _256BitMemory _2 (.Add(Add), .I(I[2]), .W(W), .R(R), .O(O[2]));
  _256BitMemory _3 (.Add(Add), .I(I[3]), .W(W), .R(R), .O(O[3]));
  _256BitMemory _4 (.Add(Add), .I(I[4]), .W(W), .R(R), .O(O[4]));
  _256BitMemory _5 (.Add(Add), .I(I[5]), .W(W), .R(R), .O(O[5]));
  _256BitMemory _6 (.Add(Add), .I(I[6]), .W(W), .R(R), .O(O[6]));
  _256BitMemory _7 (.Add(Add), .I(I[7]), .W(W), .R(R), .O(O[7]));
  _256BitMemory _8 (.Add(Add), .I(I[8]), .W(W), .R(R), .O(O[8]));
  _256BitMemory _9 (.Add(Add), .I(I[9]), .W(W), .R(R), .O(O[9]));
  _256BitMemory _10 (.Add(Add), .I(I[10]), .W(W), .R(R), .O(O[10]));
  _256BitMemory _11 (.Add(Add), .I(I[11]), .W(W), .R(R), .O(O[11]));
  _256BitMemory _12 (.Add(Add), .I(I[12]), .W(W), .R(R), .O(O[12]));
  _256BitMemory _13 (.Add(Add), .I(I[13]), .W(W), .R(R), .O(O[13]));
  _256BitMemory _14 (.Add(Add), .I(I[14]), .W(W), .R(R), .O(O[14]));
  _256BitMemory _15 (.Add(Add), .I(I[15]), .W(W), .R(R), .O(O[15]));
  _256BitMemory _16 (.Add(Add), .I(I[16]), .W(W), .R(R), .O(O[16]));
  _256BitMemory _17 (.Add(Add), .I(I[17]), .W(W), .R(R), .O(O[17]));
  _256BitMemory _18 (.Add(Add), .I(I[18]), .W(W), .R(R), .O(O[18]));
  _256BitMemory _19 (.Add(Add), .I(I[19]), .W(W), .R(R), .O(O[19]));
  _256BitMemory _20 (.Add(Add), .I(I[20]), .W(W), .R(R), .O(O[20]));
  _256BitMemory _21 (.Add(Add), .I(I[21]), .W(W), .R(R), .O(O[21]));
  _256BitMemory _22 (.Add(Add), .I(I[22]), .W(W), .R(R), .O(O[22]));
  _256BitMemory _23 (.Add(Add), .I(I[23]), .W(W), .R(R), .O(O[23]));
endmodule
