// Digital circuit 8-BitRegister.dig as structural Verilog
module _8_BitRegister (
  input  [7:0] I,
  input  W,
  input  R,
  output [7:0] O
);

  wire _8bitin1bit_1_out, and_1_out, not_1_out;
  wire [7:0] _1_bitmemorywr_1_o, delay_1_out;

  Delay #(.Bits(8), .delayTime(3)) delay_1 (.in(_1_bitmemorywr_1_o), .out(delay_1_out));
  _8BitIn1Bit _8bitin1bit_1 (.in(_1_bitmemorywr_1_o), .out(_8bitin1bit_1_out));
  Multiplexer #(.Bits(8)) multiplexer_1 (.sel(and_1_out), .in_0(delay_1_out), .in_1(I), .out(O));
  _1_BitMemoryWR _1_bitmemorywr_1 (.o(_1_bitmemorywr_1_o[0]), .i(I[0]), .y(1'b1), .w(W), .r(R), .x(1'b1));
  _1_BitMemoryWR _1_bitmemorywr_2 (.o(_1_bitmemorywr_1_o[1]), .i(I[1]), .y(1'b1), .w(W), .r(R), .x(1'b1));
  _1_BitMemoryWR _1_bitmemorywr_3 (.o(_1_bitmemorywr_1_o[2]), .i(I[2]), .y(1'b1), .w(W), .r(R), .x(1'b1));
  _1_BitMemoryWR _1_bitmemorywr_4 (.o(_1_bitmemorywr_1_o[3]), .i(I[3]), .y(1'b1), .w(W), .r(R), .x(1'b1));
  _1_BitMemoryWR _1_bitmemorywr_5 (.o(_1_bitmemorywr_1_o[4]), .i(I[4]), .y(1'b1), .w(W), .r(R), .x(1'b1));
  _1_BitMemoryWR _1_bitmemorywr_6 (.o(_1_bitmemorywr_1_o[5]), .i(I[5]), .y(1'b1), .w(W), .r(R), .x(1'b1));
  _1_BitMemoryWR _1_bitmemorywr_7 (.o(_1_bitmemorywr_1_o[6]), .i(I[6]), .y(1'b1), .w(W), .r(R), .x(1'b1));
  _1_BitMemoryWR _1_bitmemorywr_8 (.o(_1_bitmemorywr_1_o[7]), .i(I[7]), .y(1'b1), .w(W), .r(R), .x(1'b1));
  not not_1 (not_1_out, _8bitin1bit_1_out);
  and and_1 (and_1_out, W, R, not_1_out);
endmodule
