// Digital circuit PreBuiltRamConfig.dig as structural Verilog
module PreBuiltRamConfig (
  input  C_M,
  input  C_A,
  output [23:0] I,
  output [7:0] Add,
  output W,
  output RDY
);

  wire _8bitin1bit_1_out, or_1_out;
  wire [4:0] or_2_out;
  wire [7:0] \_8bitsequenzenzähler_1_add ;

  or or_1 (or_1_out, C_M, C_A);
  _8BitIn1Bit _8bitin1bit_1 (.in({3'b000, or_2_out}), .out(_8bitin1bit_1_out));
  \_8BitSequenzenzähler  \_8bitsequenzenzähler_1  (
    .C(or_1_out), .JT({8{1'b0}}), .R(_8bitin1bit_1_out), .Add(\_8bitsequenzenzähler_1_add ));  // open: Ca
  Multiplexer #(.Selector_Bits(3), .Bits(24)) multiplexer_1 (
    .sel(\_8bitsequenzenzähler_1_add [2:0]), .in_0({24{1'b0}}), .in_1({24{1'b0}}), .in_2(24'h30403),
    .in_3({24{1'b0}}), .in_4(24'h7), .in_5(24'h5), .in_6({24{1'b0}}), .in_7({24{1'b0}}), .out(I));
  not not_1 (W, _8bitin1bit_1_out);
  assign or_2_out = \_8bitsequenzenzähler_1_add [7:3] | or_2_out;  // Or or_2, 5 bits wide
  Delay #(.Bits(8), .delayTime(3)) delay_1 (.in({{5{1'b0}}, \_8bitsequenzenzähler_1_add [2:0]}), .out(Add));
  Delay #(.delayTime(3)) delay_2 (.in(_8bitin1bit_1_out), .out(RDY));

  // Notes on the sheet:
  //   OP-Code
  //   Add_A
  //   Add_B
endmodule
