// Digital circuit RamVergleich.dig as structural Verilog
module RamVergleich (
  input  Clock,
  input  Input,
  input  [1:0] Address1,
  input  [1:0] Address2,
  input  RD,
  input  WD,
  input  [1:0] RegW,
  input  WDRegW,
  output getrenntePort,
  output BlockRam_getrenntePorts,
  output BiDirektionalerPort,
  output RegisterA,
  output RegisterB,
  output ChipSelect,
  output asyncron,
  output DualPortA,
  output DualPortB
);

  RAMDualPort u_getrenntePort (.A(Address1), .Din(Input), .str(WD), .C(Clock), .ld(RD), .D(getrenntePort));
  BlockRAMDualPort u_BlockRam_getrenntePorts (
    .A(Address1), .Din(Input), .str(WD), .C(Clock), .D(BlockRam_getrenntePorts));
  RAMSinglePort u_BiDirektionalerPort (.A(Address1), .str(WD), .C(Clock), .ld(RD), .D(BiDirektionalerPort));
  RegisterFile Register (
    .Din(Input), .we(WDRegW), .Rw(RegW), .C(Clock), .Ra(Address1), .Rb(Address2), .Da(RegisterA),
    .Db(RegisterB));
  RAMSinglePortSel u_ChipSelect (.A(Address1), .CS(Clock), .WE(WD), .OE(RD), .D(ChipSelect));
  RAMDualAccess DualPort (
    .str(WD), .C(Clock), .ld(RD), .A1(Address1), .Din1(Input), .A2(Address2), .D1(DualPortA), .D2(DualPortB));
  RAMAsync u_asyncron (.A(Address1), .D(Input), .we(WD), .Q(asyncron));

  // Notes on the sheet:
  //   A2 only Read für D2 kann nicht Schreiben
endmodule
